// Logisim project 4bit_t1.circ as structural Verilog
module main (
  input  clear_ALL,
  output [3:0] out_2,
  output [7:0] out_3
);

  wire clock_1_out, controlled_buffer_3_out, controlunitv1_1_chlt, demultiplexer_2_out0,
       demultiplexer_2_out1, demultiplexer_2_out2, demultiplexer_2_out3, demultiplexer_3_out0,
       demultiplexer_3_out1, demultiplexer_3_out2, demultiplexer_3_out3, demultiplexer_4_out0,
       demultiplexer_4_out1, demultiplexer_4_out2, demultiplexer_4_out3, demultiplexer_5_out0,
       demultiplexer_5_out1, demultiplexer_5_out2, demultiplexer_5_out3, mycomparater_1_equalzero, not_1_out;
  wire [1:0] controlunitv1_1_ram_mux_addr;
  wire [2:0] controlunitv1_1_cpu_bits;
  wire [3:0] ACC_q, alu_4bit_1_cpu_out, controlled_buffer_4_out, controlled_buffer_6_out,
       controlled_buffer_7_out, controlled_buffer_8_out, controlled_buffer_9_out, controlunitv1_1_cycle_out,
       InstructionRegister_q, OutputRegister_q, ram_2_dout, ram_3_dout, ram_4_dout, ram_5_dout, RegisterA_q;
  wire [7:0] controlled_buffer_1_out, controlled_buffer_2_out, demultiplexer_1_out0, demultiplexer_1_out1,
       demultiplexer_1_out2, demultiplexer_1_out3, MemoryAddressRegister_q, ProgramCounter_q;
  wire [20:0] controlunitv1_1_controlbits;

  Counter ProgramCounter (
    .load(controlunitv1_1_controlbits[19]), .D(controlled_buffer_1_out),
    .count(controlunitv1_1_controlbits[18]), .Q(ProgramCounter_q), .clk(controlled_buffer_3_out),
    .clr(controlunitv1_1_controlbits[17]));  // open: carry, up
  Register MemoryAddressRegister (
    .D(controlled_buffer_2_out), .en(controlunitv1_1_controlbits[15]), .clk(controlled_buffer_3_out),
    .Q(MemoryAddressRegister_q), .clr(controlunitv1_1_controlbits[14]));
  Register #(.width(4)) InstructionRegister (
    .D(controlled_buffer_4_out), .en(controlunitv1_1_controlbits[9]), .clk(controlled_buffer_3_out),
    .Q(InstructionRegister_q), .clr(controlunitv1_1_controlbits[8]));
  assign controlled_buffer_1_out = controlunitv1_1_controlbits[20] ? controlled_buffer_2_out : 8'bz;  // Controlled_Buffer controlled_buffer_1
  assign controlled_buffer_2_out = controlunitv1_1_controlbits[16] ? ProgramCounter_q : 8'bz;  // Controlled_Buffer controlled_buffer_2
  assign controlled_buffer_3_out = not_1_out ? clock_1_out : 1'bz;  // Controlled_Buffer controlled_buffer_3
  Clock clock_1 (.out(clock_1_out));
  not not_1 (not_1_out, controlunitv1_1_chlt);
  controlUnitV1 controlunitv1_1 (
    .CLK(controlled_buffer_3_out), .instruction(InstructionRegister_q), .clear_ALL(clear_ALL),
    .s_equalZero(mycomparater_1_equalzero), .cHLT(controlunitv1_1_chlt),
    .cycle_out(controlunitv1_1_cycle_out), .cmdregOUT(out_2), .controlBits(controlunitv1_1_controlbits),
    .cu_address(out_3), .address(controlled_buffer_2_out), .ram_mux_addr(controlunitv1_1_ram_mux_addr),
    .cpu_bits(controlunitv1_1_cpu_bits));
  Hex_Digit_Display hex_digit_display_1 (.value(controlunitv1_1_cycle_out));  // open: dp
  Register #(.width(4)) OutputRegister (
    .D(controlled_buffer_4_out), .en(controlunitv1_1_controlbits[7]), .clk(controlled_buffer_3_out),
    .Q(OutputRegister_q), .clr(controlunitv1_1_controlbits[6]));
  Register #(.width(4)) ACC (
    .D(controlled_buffer_4_out), .en(controlunitv1_1_controlbits[1]), .clk(controlled_buffer_3_out),
    .Q(ACC_q), .clr(controlunitv1_1_controlbits[0]));
  assign controlled_buffer_4_out = controlunitv1_1_controlbits[2] ? ACC_q : 4'bz;  // Controlled_Buffer controlled_buffer_4
  Register #(.width(4)) RegisterA (
    .D(controlled_buffer_4_out), .en(controlunitv1_1_controlbits[5]), .clk(controlled_buffer_3_out),
    .Q(RegisterA_q), .clr(controlunitv1_1_controlbits[4]));
  Hex_Digit_Display hex_digit_display_2 (.value(OutputRegister_q));  // open: dp
  assign controlled_buffer_4_out = controlunitv1_1_controlbits[3] ? alu_4bit_1_cpu_out : 4'bz;  // Controlled_Buffer controlled_buffer_5
  Demultiplexer #(.select(2), .width(8)) demultiplexer_1 (
    .out0(demultiplexer_1_out0), .out1(demultiplexer_1_out1), .out2(demultiplexer_1_out2),
    .out3(demultiplexer_1_out3), .in(MemoryAddressRegister_q), .sel(controlunitv1_1_ram_mux_addr));
  Demultiplexer #(.select(2)) demultiplexer_2 (
    .out0(demultiplexer_2_out0), .out1(demultiplexer_2_out1), .out2(demultiplexer_2_out2),
    .out3(demultiplexer_2_out3), .in(controlunitv1_1_controlbits[13]), .sel(controlunitv1_1_ram_mux_addr));
  myComparater mycomparater_1 (.in_1(ACC_q), .equalZero(mycomparater_1_equalzero));
  ALU_4bit alu_4bit_1 (.a(ACC_q), .b(RegisterA_q), .opcode(controlunitv1_1_cpu_bits), .cpu_out(alu_4bit_1_cpu_out));
  Demultiplexer #(.select(2)) demultiplexer_3 (
    .out0(demultiplexer_3_out0), .out1(demultiplexer_3_out1), .out2(demultiplexer_3_out2),
    .out3(demultiplexer_3_out3), .in(controlunitv1_1_controlbits[12]), .sel(controlunitv1_1_ram_mux_addr));
  Demultiplexer #(.select(2)) demultiplexer_4 (
    .out0(demultiplexer_4_out0), .out1(demultiplexer_4_out1), .out2(demultiplexer_4_out2),
    .out3(demultiplexer_4_out3), .in(controlunitv1_1_controlbits[11]), .sel(controlunitv1_1_ram_mux_addr));
  Demultiplexer #(.select(2)) demultiplexer_5 (
    .out0(demultiplexer_5_out0), .out1(demultiplexer_5_out1), .out2(demultiplexer_5_out2),
    .out3(demultiplexer_5_out3), .in(controlunitv1_1_controlbits[10]), .sel(controlunitv1_1_ram_mux_addr));
  LED led_1 (.in(mycomparater_1_equalzero));
  RAM #(.addrWidth(10)) ram_1 ();  // open: addr, we, oe, clk, din, dout
  assign controlled_buffer_6_out = demultiplexer_4_out0 ? controlled_buffer_4_out : 4'bz;  // Controlled_Buffer controlled_buffer_6
  assign controlled_buffer_7_out = demultiplexer_4_out1 ? controlled_buffer_4_out : 4'bz;  // Controlled_Buffer controlled_buffer_7
  assign controlled_buffer_8_out = demultiplexer_4_out2 ? controlled_buffer_4_out : 4'bz;  // Controlled_Buffer controlled_buffer_8
  assign controlled_buffer_9_out = demultiplexer_4_out3 ? controlled_buffer_4_out : 4'bz;  // Controlled_Buffer controlled_buffer_9
  RAM #(.asyncread("true"), .dataWidth(4), .\type ("nonvolatile")) ram_2 (
    .addr(demultiplexer_1_out0), .we(demultiplexer_2_out0), .oe(demultiplexer_3_out0),
    .clk(controlled_buffer_3_out), .din(controlled_buffer_6_out), .dout(ram_2_dout));
  RAM #(.asyncread("true"), .dataWidth(4), .\type ("nonvolatile")) ram_3 (
    .addr(demultiplexer_1_out1), .we(demultiplexer_2_out1), .oe(demultiplexer_3_out1),
    .clk(controlled_buffer_3_out), .din(controlled_buffer_7_out), .dout(ram_3_dout));
  RAM #(.asyncread("true"), .dataWidth(4), .\type ("nonvolatile")) ram_4 (
    .addr(demultiplexer_1_out2), .we(demultiplexer_2_out2), .oe(demultiplexer_3_out2),
    .clk(controlled_buffer_3_out), .din(controlled_buffer_8_out), .dout(ram_4_dout));
  RAM #(.asyncread("true"), .dataWidth(4), .\type ("nonvolatile")) ram_5 (
    .addr(demultiplexer_1_out3), .we(demultiplexer_2_out3), .oe(demultiplexer_3_out3),
    .clk(controlled_buffer_3_out), .din(controlled_buffer_9_out), .dout(ram_5_dout));
  assign controlled_buffer_4_out = demultiplexer_5_out0 ? ram_2_dout : 4'bz;  // Controlled_Buffer controlled_buffer_10
  assign controlled_buffer_4_out = demultiplexer_5_out1 ? ram_3_dout : 4'bz;  // Controlled_Buffer controlled_buffer_11
  assign controlled_buffer_4_out = demultiplexer_5_out2 ? ram_4_dout : 4'bz;  // Controlled_Buffer controlled_buffer_12
  assign controlled_buffer_4_out = demultiplexer_5_out3 ? ram_5_dout : 4'bz;  // Controlled_Buffer controlled_buffer_13

  // Notes on the sheet:
  //   PC-MAR-RAM-IR
endmodule

module ALU_4bit (
  input  [3:0] a,
  input  [3:0] b,
  input  [2:0] opcode,
  output [3:0] cpu_out
);

  wire [3:0] adder_1_out, adder_2_out, and_1_out, not_1_out, or_1_out, subtractor_1_out, subtractor_2_out,
       xor_1_out;

  Adder #(.width(4)) adder_1 (.a(a), .b(b), .out(adder_1_out));  // open: cin, cout
  Subtractor #(.width(4)) subtractor_1 (.a(a), .b(b), .out(subtractor_1_out));  // open: bin, bout
  assign and_1_out = a & b;  // AND_Gate and_1, 4 bits wide
  assign or_1_out = a | b;  // OR_Gate or_1, 4 bits wide
  assign not_1_out = ~a;  // NOT_Gate not_1, 4 bits wide
  assign xor_1_out = a ^ b;  // XOR_Gate xor_1, 4 bits wide
  Adder #(.width(4)) adder_2 (.a(a), .b(4'b0001), .out(adder_2_out));  // open: cin, cout
  Subtractor #(.width(4)) subtractor_2 (.a(a), .b(4'b0001), .out(subtractor_2_out));  // open: bin, bout
  Multiplexer #(.select(3), .width(4)) multiplexer_1 (
    .in0(adder_1_out), .in1(subtractor_1_out), .in2(and_1_out), .in3(or_1_out), .in4(xor_1_out),
    .in5(not_1_out), .in6(adder_2_out), .in7(subtractor_2_out), .out(cpu_out), .sel(opcode));
endmodule

module controlUnitV1 (
  input  CLK,
  input  [3:0] instruction,
  input  clear_ALL,
  input  s_equalZero,
  output cHLT,
  output [3:0] cycle_out,
  output [3:0] cmdregOUT,
  output [20:0] controlBits,
  output [7:0] cu_address,
  output [7:0] address,
  output [1:0] ram_mux_addr,
  output [2:0] cpu_bits
);

  wire ADD, addr_out_out, and_1_out, and_3_out, and_4_out, and_5_out, and_6_out, and_7_out, and_8_out,
       and_9_out, and_10_out, and_11_out, and_12_out, and_13_out, and_14_out, and_15_out, and_16_out,
       and_17_out, and_18_out, and_19_out, and_20_out, cAND, cNOT, cOR, cOUT, CRA, cXOR, DEC, decoder_2_out0,
       decoder_2_out1, decoder_2_out2, decoder_2_out3, decoder_2_out4, decoder_2_out5, decoder_2_out6,
       decoder_2_out7, decoder_2_out8, decoder_2_out9, decoder_2_out10, decoder_2_out11, decoder_2_out12,
       HLT, INC, JEZ, JMP, JNZ, LDA, left_bit_we_out, mux_bit_out, not_1_out, or_1_out, or_2_out, or_3_out,
       or_4_out, or_5_out, or_6_out, ram_mux_enb, right_bit_we_out, STA, SUB, t1_load_out, t6_load_out,
       t8_out, t9_out;
  wire [3:0] demultiplexer_1_out0, demultiplexer_1_out1;

  Register #(.width(4)) command (.D(instruction), .en(decoder_2_out2), .clk(and_1_out), .Q(cmdregOUT), .clr(clear_ALL));
  Demultiplexer #(.width(4)) demultiplexer_1 (
    .out0(demultiplexer_1_out0), .out1(demultiplexer_1_out1), .in(instruction), .sel(mux_bit_out));
  Decoder #(.enable("false"), .select(4)) decoder_1 (
    .out0(HLT), .out1(LDA), .out2(STA), .out3(ADD), .out4(SUB), .out5(cAND), .out6(cOR), .out7(cXOR),
    .out8(cNOT), .out9(INC), .out10(DEC), .out11(JEZ), .out12(JNZ), .out13(CRA), .out14(JMP), .out15(cOUT),
    .sel(cmdregOUT));
  Register #(.width(4)) right_bit (
    .D(demultiplexer_1_out0), .en(right_bit_we_out), .clk(CLK), .Q(cu_address[3:0]), .clr(clear_ALL));
  Register #(.width(4)) left_bit (
    .D(demultiplexer_1_out1), .en(left_bit_we_out), .clk(CLK), .Q(cu_address[7:4]), .clr(clear_ALL));
  or addr_out (addr_out_out, t8_out, and_9_out, and_15_out, and_16_out, and_17_out);
  or left_bit_we (left_bit_we_out, and_4_out, and_20_out);
  buf right_bit_we (right_bit_we_out, t6_load_out);  // OR_Gate
  or mux_bit (mux_bit_out, and_4_out, and_20_out);
  or pc_input_get_addressline (controlBits[20], 1'b0, or_6_out);
  or pc_loadData_enable (controlBits[19], 1'b0, or_6_out);
  or pc_enable (controlBits[18], decoder_2_out0, or_3_out);
  or pc_output_to_addressline (controlBits[16], decoder_2_out0, or_3_out);
  or mar_we (controlBits[15], decoder_2_out0, or_3_out, t8_out, and_7_out, and_9_out);
  or ram_write_enable (controlBits[13], 1'b0, and_8_out);
  or ram_output_enable (controlBits[12], decoder_2_out1, or_2_out, t9_out, and_10_out);
  or ram_input_in_dataline (controlBits[11], 1'b0, and_8_out);
  or ram_output_to_dataline (controlBits[10], decoder_2_out1, or_2_out, t9_out, and_10_out);
  or ins_we (controlBits[9], decoder_2_out1, or_2_out);
  or regOUT_we (controlBits[7], 1'b0, and_14_out);
  or rega_we (controlBits[5], 1'b0, and_10_out);
  or cpu_output_to_dataline (controlBits[3], 1'b0, and_11_out, and_12_out, and_13_out);
  or acc_output_to_dataLine (controlBits[2], 1'b0, and_8_out, and_14_out);
  or ACC_WE (controlBits[1], 1'b0, t9_out, and_11_out, and_12_out, and_13_out);
  assign address = addr_out_out ? cu_address : 8'bz;  // Controlled_Buffer controlled_buffer_1
  Register #(.width(2)) register_1 (
    .D(cu_address[5:4]), .en(ram_mux_enb), .clk(CLK), .Q(ram_mux_addr), .clr(clear_ALL));
  and and_1 (and_1_out, ~cHLT, CLK);  // AND_Gate
  Counter #(.max('hf), .width(4)) counter_1 (
    .count(and_1_out), .Q(cycle_out), .clk(and_1_out), .clr(decoder_2_out12));  // open: load, D, carry, up
  Decoder #(.enable("false"), .select(4)) decoder_2 (
    .out0(decoder_2_out0), .out1(decoder_2_out1), .out2(decoder_2_out2), .out3(decoder_2_out3),
    .out4(decoder_2_out4), .out5(decoder_2_out5), .out6(decoder_2_out6), .out7(decoder_2_out7),
    .out8(decoder_2_out8), .out9(decoder_2_out9), .out10(decoder_2_out10), .out11(decoder_2_out11),
    .out12(decoder_2_out12), .sel(cycle_out));  // open: out13, out14, out15
  or or_1 (or_1_out, LDA, STA, ADD, SUB, cAND, cOR, cXOR, cNOT, JMP, JEZ, JNZ);
  Hex_Digit_Display hex_digit_display_1 (.value(cycle_out));  // open: dp
  and and_2 (cHLT, decoder_2_out3, HLT);
  or or_2 (or_2_out, and_19_out, and_6_out, and_3_out);
  or or_3 (or_3_out, and_18_out, and_5_out, t1_load_out);
  and t1_load (t1_load_out, decoder_2_out3, or_1_out);
  and and_3 (and_3_out, or_1_out, decoder_2_out4);
  and and_4 (and_4_out, or_1_out, decoder_2_out5);
  and and_5 (and_5_out, or_1_out, decoder_2_out6);
  and and_6 (and_6_out, or_1_out, decoder_2_out7);
  and t6_load (t6_load_out, or_1_out, decoder_2_out8);
  and t8 (t8_out, LDA, decoder_2_out9);
  and t9 (t9_out, LDA, decoder_2_out10);
  and and_7 (and_7_out, STA, decoder_2_out9);
  and and_8 (and_8_out, STA, decoder_2_out10);
  assign cpu_bits = ADD ? 3'b000 : 3'bz;  // Controlled_Buffer controlled_buffer_2
  or or_4 (or_4_out, cXOR, cOR, cAND, SUB, ADD);
  assign cpu_bits = SUB ? 3'b001 : 3'bz;  // Controlled_Buffer controlled_buffer_3
  and and_9 (and_9_out, decoder_2_out9, or_4_out);
  and and_10 (and_10_out, or_4_out, decoder_2_out10);
  and and_11 (and_11_out, or_4_out, decoder_2_out11);
  assign cpu_bits = cAND ? 3'b010 : 3'bz;  // Controlled_Buffer controlled_buffer_4
  assign cpu_bits = cOR ? 3'b011 : 3'bz;  // Controlled_Buffer controlled_buffer_5
  and and_12 (and_12_out, decoder_2_out9, cNOT);
  assign cpu_bits = cXOR ? 3'b100 : 3'bz;  // Controlled_Buffer controlled_buffer_6
  assign cpu_bits = cNOT ? 3'b101 : 3'bz;  // Controlled_Buffer controlled_buffer_7
  assign cpu_bits = INC ? 3'b110 : 3'bz;  // Controlled_Buffer controlled_buffer_8
  and and_13 (and_13_out, decoder_2_out9, or_5_out);
  or or_5 (or_5_out, INC, DEC);
  assign cpu_bits = DEC ? 3'b111 : 3'bz;  // Controlled_Buffer controlled_buffer_9
  and and_14 (and_14_out, decoder_2_out3, cOUT);
  and and_15 (and_15_out, decoder_2_out9, JMP);
  or or_6 (or_6_out, and_15_out, and_16_out, and_17_out);
  and and_16 (and_16_out, decoder_2_out9, JEZ, s_equalZero);
  not not_1 (not_1_out, s_equalZero);
  and and_17 (and_17_out, decoder_2_out9, JNZ, not_1_out);
  and and_18 (and_18_out, decoder_2_out3, CRA);
  and and_19 (and_19_out, CRA, decoder_2_out4);
  and and_20 (and_20_out, CRA, decoder_2_out5);
  and and_21 (ram_mux_enb, CRA, decoder_2_out6);

  assign {controlBits[17], controlBits[14], controlBits[8], controlBits[6], controlBits[4], controlBits[0]} = {6{clear_ALL}};

  // Other names for the same wires on the sheet: address_t[3:0] = instruction

  // Notes on the sheet:
  //   INSTRUCTION DECODER
  //   CONTROL BITS
  //   RING COUNTER
  //   t8-t9 for LDA
  //   //putting next 4-bit to ins reg
  //   pc++;mar = pc;
  //   //taking next 4-bit
  //   first_6 AND GATE: load (left-right bits) address
  //   First load left bits :: Second load right bits
  //   ins = ram;
endmodule

module myComparater (
  input  [3:0] in_1,
  output equalZero
);

  wire and_1_out, and_2_out, and_3_out, and_4_out, and_5_out, and_6_out;

  and and_1 (and_1_out, ~1'b0, ~in_1[0]);  // AND_Gate
  and and_2 (and_2_out, ~1'b0, ~in_1[1]);  // AND_Gate
  and and_3 (and_3_out, ~1'b0, ~in_1[2]);  // AND_Gate
  and and_4 (and_4_out, ~1'b0, ~in_1[3]);  // AND_Gate
  and and_5 (and_5_out, and_1_out, and_2_out);
  and and_6 (and_6_out, and_3_out, and_4_out);
  and and_7 (equalZero, and_5_out, and_6_out);
endmodule
